# Fritzing sketch project3 (saved by Fritzing 0.9.3b)
breadboards: 2

parts:
  Part1 = Arduino Uno (Rev3) - ICSP
  LED1 = LEDs [package=led10mm]
  diode1 = EK8443 IR diode [package=led5mm]
  R1 = Resistor [tolerance=±5% resistance=220 package=THT]
  R2 = Resistor [tolerance=±5% resistance=2.2k package=THT]

nets:
  N1: Part1.D2, diode1.C, R2.Pin_0
  N2: Part1.5V, LED1.A, diode1.A
  N3: Part1.GND, R1.Pin_0, R2.Pin_1
  N4: LED1.C, R1.Pin_1
